// Logisim project Contadores Síncronos.circ as structural Verilog: 19 circuits, main circuit Contador síncrono crescente
module main (
  input  in_1,
  output Q3,
  output Q2,
  output Q1,
  output Q0
);

  wire bin_2_seteseg_1_a_2, bin_2_seteseg_1_b_2, bin_2_seteseg_1_c_2, bin_2_seteseg_1_d_2, bin_2_seteseg_1_e,
       bin_2_seteseg_1_f, bin_2_seteseg_1_g, n1_2_3_5_8_9_b_f_5_1_j0, n1_2_3_5_8_9_b_f_5_1_j1,
       n1_2_3_5_8_9_b_f_5_1_j2, n1_2_3_5_8_9_b_f_5_1_j3, n1_2_3_5_8_9_b_f_5_1_k0, n1_2_3_5_8_9_b_f_5_1_k1,
       n1_2_3_5_8_9_b_f_5_1_k2, n1_2_3_5_8_9_b_f_5_1_k3;

  JK_com_sr_do_sistema jk_com_sr_do_sistema_1 (
    .J(n1_2_3_5_8_9_b_f_5_1_j0), .Clock(in_1), .K(n1_2_3_5_8_9_b_f_5_1_k0), .Q(Q3));  // open: PRS, CLR, nQ
  JK_com_sr_do_sistema jk_com_sr_do_sistema_2 (
    .J(n1_2_3_5_8_9_b_f_5_1_j1), .Clock(in_1), .K(n1_2_3_5_8_9_b_f_5_1_k1), .Q(Q2));  // open: PRS, CLR, nQ
  JK_com_sr_do_sistema jk_com_sr_do_sistema_3 (
    .J(n1_2_3_5_8_9_b_f_5_1_j2), .Clock(in_1), .K(n1_2_3_5_8_9_b_f_5_1_k2), .Q(Q1));  // open: PRS, CLR, nQ
  JK_com_sr_do_sistema jk_com_sr_do_sistema_4 (
    .J(n1_2_3_5_8_9_b_f_5_1_j3), .Clock(in_1), .K(n1_2_3_5_8_9_b_f_5_1_k3), .Q(Q0));  // open: PRS, CLR, nQ
  _1_2_3_5_8_9_B_F_5 u_1_2_3_5_8_9_b_f_5_1 (
    .Q0(Q0), .Q1(Q1), .Q2(Q2), .Q3(Q3), .J3(n1_2_3_5_8_9_b_f_5_1_j3), .K3(n1_2_3_5_8_9_b_f_5_1_k3),
    .J2(n1_2_3_5_8_9_b_f_5_1_j2), .K2(n1_2_3_5_8_9_b_f_5_1_k2), .J1(n1_2_3_5_8_9_b_f_5_1_j1),
    .K1(n1_2_3_5_8_9_b_f_5_1_k1), .J0(n1_2_3_5_8_9_b_f_5_1_j0), .K0(n1_2_3_5_8_9_b_f_5_1_k0));
  bin_2_seteseg bin_2_seteseg_1 (
    .D(Q0), .C(Q1), .B(Q2), .A(Q3), .a_2(bin_2_seteseg_1_a_2), .b_2(bin_2_seteseg_1_b_2),
    .c_2(bin_2_seteseg_1_c_2), .d_2(bin_2_seteseg_1_d_2), .e(bin_2_seteseg_1_e), .f(bin_2_seteseg_1_f),
    .g(bin_2_seteseg_1_g));
  _7_Segment_Display u_7_segment_display_1 (
    .g(bin_2_seteseg_1_g), .f(bin_2_seteseg_1_f), .a(bin_2_seteseg_1_a_2), .b(bin_2_seteseg_1_b_2),
    .e(bin_2_seteseg_1_e), .d(bin_2_seteseg_1_d_2), .c(bin_2_seteseg_1_c_2));  // open: dp
endmodule

module \Contador_síncrono_crescente  (
  input  in_1,
  output Q3,
  output Q2,
  output Q1,
  output Q0
);

  wire bin_2_seteseg_1_a_2, bin_2_seteseg_1_b_2, bin_2_seteseg_1_c_2, bin_2_seteseg_1_d_2, bin_2_seteseg_1_e,
       bin_2_seteseg_1_f, bin_2_seteseg_1_g, sinc_crescente_comb_1_j0, sinc_crescente_comb_1_j1,
       sinc_crescente_comb_1_j2, sinc_crescente_comb_1_j3, sinc_crescente_comb_1_k0,
       sinc_crescente_comb_1_k1, sinc_crescente_comb_1_k2, sinc_crescente_comb_1_k3;

  JK_com_sr_do_sistema jk_com_sr_do_sistema_1 (
    .J(sinc_crescente_comb_1_j0), .Clock(in_1), .K(sinc_crescente_comb_1_k0), .Q(Q3));  // open: PRS, CLR, nQ
  JK_com_sr_do_sistema jk_com_sr_do_sistema_2 (
    .J(sinc_crescente_comb_1_j1), .Clock(in_1), .K(sinc_crescente_comb_1_k1), .Q(Q2));  // open: PRS, CLR, nQ
  JK_com_sr_do_sistema jk_com_sr_do_sistema_3 (
    .J(sinc_crescente_comb_1_j2), .Clock(in_1), .K(sinc_crescente_comb_1_k2), .Q(Q1));  // open: PRS, CLR, nQ
  JK_com_sr_do_sistema jk_com_sr_do_sistema_4 (
    .J(sinc_crescente_comb_1_j3), .Clock(in_1), .K(sinc_crescente_comb_1_k3), .Q(Q0));  // open: PRS, CLR, nQ
  sinc_crescente_comb sinc_crescente_comb_1 (
    .Q0(Q0), .Q1(Q1), .Q2(Q2), .Q3(Q3), .J3(sinc_crescente_comb_1_j3), .K3(sinc_crescente_comb_1_k3),
    .J2(sinc_crescente_comb_1_j2), .K2(sinc_crescente_comb_1_k2), .J1(sinc_crescente_comb_1_j1),
    .K1(sinc_crescente_comb_1_k1), .J0(sinc_crescente_comb_1_j0), .K0(sinc_crescente_comb_1_k0));
  bin_2_seteseg bin_2_seteseg_1 (
    .D(Q0), .C(Q1), .B(Q2), .A(Q3), .a_2(bin_2_seteseg_1_a_2), .b_2(bin_2_seteseg_1_b_2),
    .c_2(bin_2_seteseg_1_c_2), .d_2(bin_2_seteseg_1_d_2), .e(bin_2_seteseg_1_e), .f(bin_2_seteseg_1_f),
    .g(bin_2_seteseg_1_g));
  _7_Segment_Display u_7_segment_display_1 (
    .g(bin_2_seteseg_1_g), .f(bin_2_seteseg_1_f), .a(bin_2_seteseg_1_a_2), .b(bin_2_seteseg_1_b_2),
    .e(bin_2_seteseg_1_e), .d(bin_2_seteseg_1_d_2), .c(bin_2_seteseg_1_c_2));  // open: dp
endmodule

module \Contador_síncrono_decrescente  (
  input  in_1,
  output out_2,
  output out_3,
  output out_4,
  output out_5
);

  wire bin_2_seteseg_1_a_2, bin_2_seteseg_1_b_2, bin_2_seteseg_1_c_2, bin_2_seteseg_1_d_2, bin_2_seteseg_1_e,
       bin_2_seteseg_1_f, bin_2_seteseg_1_g, jk_com_preset_e_clear_1_p1, jk_com_preset_e_clear_1_p3,
       jk_com_preset_e_clear_2_p1, jk_com_preset_e_clear_2_p3, jk_com_preset_e_clear_3_p1,
       jk_com_preset_e_clear_3_p3, jk_com_preset_e_clear_4_p1, jk_com_preset_e_clear_4_p3;

  // JK_com_preset_e_clear jk_com_preset_e_clear_1: pin names not known; wires that end beside it: jk_com_preset_e_clear_1_p1, in_1, jk_com_preset_e_clear_1_p3, out_2
  // JK_com_preset_e_clear jk_com_preset_e_clear_2: pin names not known; wires that end beside it: jk_com_preset_e_clear_2_p1, in_1, jk_com_preset_e_clear_2_p3, out_3
  // JK_com_preset_e_clear jk_com_preset_e_clear_3: pin names not known; wires that end beside it: jk_com_preset_e_clear_3_p1, in_1, jk_com_preset_e_clear_3_p3, out_4
  // JK_com_preset_e_clear jk_com_preset_e_clear_4: pin names not known; wires that end beside it: jk_com_preset_e_clear_4_p1, in_1, jk_com_preset_e_clear_4_p3, out_5
  sinc_decrescente_comb sinc_decrescente_comb_1 (
    .Q0(out_5), .Q1(out_4), .Q2(out_3), .Q3(out_2), .J3(jk_com_preset_e_clear_4_p1),
    .K3(jk_com_preset_e_clear_4_p3), .J2(jk_com_preset_e_clear_3_p1), .K2(jk_com_preset_e_clear_3_p3),
    .J1(jk_com_preset_e_clear_2_p1), .K1(jk_com_preset_e_clear_2_p3), .J0(jk_com_preset_e_clear_1_p1),
    .K0(jk_com_preset_e_clear_1_p3));
  bin_2_seteseg bin_2_seteseg_1 (
    .D(out_5), .C(out_4), .B(out_3), .A(out_2), .a_2(bin_2_seteseg_1_a_2), .b_2(bin_2_seteseg_1_b_2),
    .c_2(bin_2_seteseg_1_c_2), .d_2(bin_2_seteseg_1_d_2), .e(bin_2_seteseg_1_e), .f(bin_2_seteseg_1_f),
    .g(bin_2_seteseg_1_g));
  _7_Segment_Display u_7_segment_display_1 (
    .g(bin_2_seteseg_1_g), .f(bin_2_seteseg_1_f), .a(bin_2_seteseg_1_a_2), .b(bin_2_seteseg_1_b_2),
    .e(bin_2_seteseg_1_e), .d(bin_2_seteseg_1_d_2), .c(bin_2_seteseg_1_c_2));  // open: dp
endmodule

module \Contador_de_década_síncrono  (
  output out_1,
  output out_2,
  output out_3,
  output out_4
);

  wire bin_2_seteseg_1_a_2, bin_2_seteseg_1_b_2, bin_2_seteseg_1_c_2, bin_2_seteseg_1_d_2, bin_2_seteseg_1_e,
       bin_2_seteseg_1_f, bin_2_seteseg_1_g, clock_1_out, jk_com_preset_e_clear_1_p1,
       jk_com_preset_e_clear_1_p3, jk_com_preset_e_clear_2_p1, jk_com_preset_e_clear_2_p3,
       jk_com_preset_e_clear_3_p1, jk_com_preset_e_clear_3_p3, jk_com_preset_e_clear_4_p1,
       jk_com_preset_e_clear_4_p3;

  Clock clock_1 (.out(clock_1_out));
  // JK_com_preset_e_clear jk_com_preset_e_clear_1: pin names not known; wires that end beside it: jk_com_preset_e_clear_1_p1, clock_1_out, jk_com_preset_e_clear_1_p3, out_1
  // JK_com_preset_e_clear jk_com_preset_e_clear_2: pin names not known; wires that end beside it: jk_com_preset_e_clear_2_p1, clock_1_out, jk_com_preset_e_clear_2_p3, out_2
  // JK_com_preset_e_clear jk_com_preset_e_clear_3: pin names not known; wires that end beside it: jk_com_preset_e_clear_3_p1, clock_1_out, jk_com_preset_e_clear_3_p3, out_3
  // JK_com_preset_e_clear jk_com_preset_e_clear_4: pin names not known; wires that end beside it: jk_com_preset_e_clear_4_p1, clock_1_out, jk_com_preset_e_clear_4_p3, out_4
  sinc_decada_comb sinc_decada_comb_1 (
    .Q0(out_4), .Q1(out_3), .Q2(out_2), .Q3(out_1), .J3(jk_com_preset_e_clear_4_p1),
    .K3(jk_com_preset_e_clear_4_p3), .J2(jk_com_preset_e_clear_3_p1), .K2(jk_com_preset_e_clear_3_p3),
    .J1(jk_com_preset_e_clear_2_p1), .K1(jk_com_preset_e_clear_2_p3), .J0(jk_com_preset_e_clear_1_p1),
    .K0(jk_com_preset_e_clear_1_p3));
  bin_2_seteseg bin_2_seteseg_1 (
    .D(out_4), .C(out_3), .B(out_2), .A(out_1), .a_2(bin_2_seteseg_1_a_2), .b_2(bin_2_seteseg_1_b_2),
    .c_2(bin_2_seteseg_1_c_2), .d_2(bin_2_seteseg_1_d_2), .e(bin_2_seteseg_1_e), .f(bin_2_seteseg_1_f),
    .g(bin_2_seteseg_1_g));
  _7_Segment_Display u_7_segment_display_1 (
    .g(bin_2_seteseg_1_g), .f(bin_2_seteseg_1_f), .a(bin_2_seteseg_1_a_2), .b(bin_2_seteseg_1_b_2),
    .e(bin_2_seteseg_1_e), .d(bin_2_seteseg_1_d_2), .c(bin_2_seteseg_1_c_2));  // open: dp
endmodule

module \Contador_síncrono_0_a_N  (
  input  in_1,
  input  [3:0] in_2,
  output out_3,
  output out_4,
  output out_5,
  output out_6
);

  wire bin_2_seteseg_1_a_2, bin_2_seteseg_1_b_2, bin_2_seteseg_1_c_2, bin_2_seteseg_1_d_2, bin_2_seteseg_1_e,
       bin_2_seteseg_1_f, bin_2_seteseg_1_g, bin_2_seteseg_2_a_2, bin_2_seteseg_2_b_2, bin_2_seteseg_2_c_2,
       bin_2_seteseg_2_d_2, bin_2_seteseg_2_e, bin_2_seteseg_2_f, bin_2_seteseg_2_g,
       jk_com_preset_e_clear_1_p1, jk_com_preset_e_clear_1_p3, jk_com_preset_e_clear_2_p1,
       jk_com_preset_e_clear_2_p3, jk_com_preset_e_clear_3_p1, jk_com_preset_e_clear_3_p3,
       jk_com_preset_e_clear_4_p1, jk_com_preset_e_clear_4_p3, n0_a_n_comb_1_clear;

  // NOT_Gate not_1 has open pins: in=n0_a_n_comb_1_clear, out=open
  // JK_com_preset_e_clear jk_com_preset_e_clear_1: pin names not known; wires that end beside it: jk_com_preset_e_clear_1_p1, in_1, jk_com_preset_e_clear_1_p3, out_3
  // JK_com_preset_e_clear jk_com_preset_e_clear_2: pin names not known; wires that end beside it: jk_com_preset_e_clear_2_p1, in_1, jk_com_preset_e_clear_2_p3, out_4
  // NOT_Gate not_2 has open pins: in=n0_a_n_comb_1_clear, out=open
  // JK_com_preset_e_clear jk_com_preset_e_clear_3: pin names not known; wires that end beside it: jk_com_preset_e_clear_3_p1, in_1, jk_com_preset_e_clear_3_p3, out_5
  // NOT_Gate not_3 has open pins: in=n0_a_n_comb_1_clear, out=open
  // JK_com_preset_e_clear jk_com_preset_e_clear_4: pin names not known; wires that end beside it: jk_com_preset_e_clear_4_p1, in_1, jk_com_preset_e_clear_4_p3, out_6
  // NOT_Gate not_4 has open pins: in=n0_a_n_comb_1_clear, out=open
  _0_a_n_comb u_0_a_n_comb_1 (
    .CLEAR(n0_a_n_comb_1_clear), .Q3(out_6), .Q2(out_5), .Q1(out_4), .Q0(out_3), .N0(in_2[0]), .N1(in_2[1]),
    .N2(in_2[2]), .N3(in_2[3]));
  sinc_crescente_comb sinc_crescente_comb_1 (
    .Q0(out_6), .Q1(out_5), .Q2(out_4), .Q3(out_3), .J3(jk_com_preset_e_clear_4_p1),
    .K3(jk_com_preset_e_clear_4_p3), .J2(jk_com_preset_e_clear_3_p1), .K2(jk_com_preset_e_clear_3_p3),
    .J1(jk_com_preset_e_clear_2_p1), .K1(jk_com_preset_e_clear_2_p3), .J0(jk_com_preset_e_clear_1_p1),
    .K0(jk_com_preset_e_clear_1_p3));
  bin_2_seteseg bin_2_seteseg_1 (
    .D(out_6), .C(out_5), .B(out_4), .A(out_3), .a_2(bin_2_seteseg_1_a_2), .b_2(bin_2_seteseg_1_b_2),
    .c_2(bin_2_seteseg_1_c_2), .d_2(bin_2_seteseg_1_d_2), .e(bin_2_seteseg_1_e), .f(bin_2_seteseg_1_f),
    .g(bin_2_seteseg_1_g));
  bin_2_seteseg bin_2_seteseg_2 (
    .D(in_2[3]), .C(in_2[2]), .B(in_2[1]), .A(in_2[0]), .a_2(bin_2_seteseg_2_a_2), .b_2(bin_2_seteseg_2_b_2),
    .c_2(bin_2_seteseg_2_c_2), .d_2(bin_2_seteseg_2_d_2), .e(bin_2_seteseg_2_e), .f(bin_2_seteseg_2_f),
    .g(bin_2_seteseg_2_g));
  _7_Segment_Display u_7_segment_display_1 (
    .g(bin_2_seteseg_1_g), .f(bin_2_seteseg_1_f), .a(bin_2_seteseg_1_a_2), .b(bin_2_seteseg_1_b_2),
    .e(bin_2_seteseg_1_e), .d(bin_2_seteseg_1_d_2), .c(bin_2_seteseg_1_c_2));  // open: dp
  _7_Segment_Display u_7_segment_display_2 (
    .g(bin_2_seteseg_2_g), .f(bin_2_seteseg_2_f), .a(bin_2_seteseg_2_a_2), .b(bin_2_seteseg_2_b_2),
    .e(bin_2_seteseg_2_e), .d(bin_2_seteseg_2_d_2), .c(bin_2_seteseg_2_c_2));  // open: dp
endmodule

// N a 0
module \Contador_síncrono_N_a_0  (
  input  CLOCK,
  input  [3:0] N,
  output out_3,
  output out_4,
  output out_5,
  output out_6
);

  wire bin_2_seteseg_1_a_2, bin_2_seteseg_1_b_2, bin_2_seteseg_1_c_2, bin_2_seteseg_1_d_2, bin_2_seteseg_1_e,
       bin_2_seteseg_1_f, bin_2_seteseg_1_g, bin_2_seteseg_2_a_2, bin_2_seteseg_2_b_2, bin_2_seteseg_2_c_2,
       bin_2_seteseg_2_d_2, bin_2_seteseg_2_e, bin_2_seteseg_2_f, bin_2_seteseg_2_g,
       jk_com_preset_e_clear_1_p1, jk_com_preset_e_clear_1_p3, jk_com_preset_e_clear_2_p1,
       jk_com_preset_e_clear_2_p3, jk_com_preset_e_clear_3_p1, jk_com_preset_e_clear_3_p3,
       jk_com_preset_e_clear_4_p1, jk_com_preset_e_clear_4_p3, LOAD_out, n_a_0_1_c0, n_a_0_1_c1, n_a_0_1_c2,
       n_a_0_1_c3, n_a_0_1_p0, n_a_0_1_p1, n_a_0_1_p2, n_a_0_1_p3;

  Button LOAD (.out(LOAD_out));
  // JK_com_preset_e_clear jk_com_preset_e_clear_1: pin names not known; wires that end beside it: jk_com_preset_e_clear_1_p1, CLOCK, jk_com_preset_e_clear_1_p3, out_3
  // NOT_Gate not_1 has open pins: in=n_a_0_1_p3, out=open
  // NOT_Gate not_2 has open pins: in=n_a_0_1_c3, out=open
  n_a_0 n_a_0_1 (
    .LOAD(LOAD_out), .P3(n_a_0_1_p3), .C3(n_a_0_1_c3), .P2(n_a_0_1_p2), .C2(n_a_0_1_c2), .P1(n_a_0_1_p1),
    .C1(n_a_0_1_c1), .P0(n_a_0_1_p0), .C0(n_a_0_1_c0), .N3(N[3]), .N2(N[2]), .N1(N[1]), .N0(N[0]));
  // JK_com_preset_e_clear jk_com_preset_e_clear_2: pin names not known; wires that end beside it: jk_com_preset_e_clear_2_p1, CLOCK, jk_com_preset_e_clear_2_p3, out_4
  // NOT_Gate not_3 has open pins: in=n_a_0_1_c2, out=open
  // NOT_Gate not_4 has open pins: in=n_a_0_1_p2, out=open
  bin_2_seteseg bin_2_seteseg_1 (
    .D(N[3]), .C(N[2]), .B(N[1]), .A(N[0]), .a_2(bin_2_seteseg_1_a_2), .b_2(bin_2_seteseg_1_b_2),
    .c_2(bin_2_seteseg_1_c_2), .d_2(bin_2_seteseg_1_d_2), .e(bin_2_seteseg_1_e), .f(bin_2_seteseg_1_f),
    .g(bin_2_seteseg_1_g));
  // JK_com_preset_e_clear jk_com_preset_e_clear_3: pin names not known; wires that end beside it: jk_com_preset_e_clear_3_p1, CLOCK, jk_com_preset_e_clear_3_p3, out_5
  // NOT_Gate not_5 has open pins: in=n_a_0_1_c1, out=open
  // NOT_Gate not_6 has open pins: in=n_a_0_1_p1, out=open
  _7_Segment_Display u_7_segment_display_1 (
    .g(bin_2_seteseg_1_g), .f(bin_2_seteseg_1_f), .a(bin_2_seteseg_1_a_2), .b(bin_2_seteseg_1_b_2),
    .e(bin_2_seteseg_1_e), .d(bin_2_seteseg_1_d_2), .c(bin_2_seteseg_1_c_2));  // open: dp
  // JK_com_preset_e_clear jk_com_preset_e_clear_4: pin names not known; wires that end beside it: jk_com_preset_e_clear_4_p1, CLOCK, jk_com_preset_e_clear_4_p3, out_6
  // NOT_Gate not_7 has open pins: in=n_a_0_1_c0, out=open
  // NOT_Gate not_8 has open pins: in=n_a_0_1_p0, out=open
  sinc_decrescente_comb sinc_decrescente_comb_1 (
    .Q0(out_6), .Q1(out_5), .Q2(out_4), .Q3(out_3), .J3(jk_com_preset_e_clear_4_p1),
    .K3(jk_com_preset_e_clear_4_p3), .J2(jk_com_preset_e_clear_3_p1), .K2(jk_com_preset_e_clear_3_p3),
    .J1(jk_com_preset_e_clear_2_p1), .K1(jk_com_preset_e_clear_2_p3), .J0(jk_com_preset_e_clear_1_p1),
    .K0(jk_com_preset_e_clear_1_p3));
  bin_2_seteseg bin_2_seteseg_2 (
    .D(out_6), .C(out_5), .B(out_4), .A(out_3), .a_2(bin_2_seteseg_2_a_2), .b_2(bin_2_seteseg_2_b_2),
    .c_2(bin_2_seteseg_2_c_2), .d_2(bin_2_seteseg_2_d_2), .e(bin_2_seteseg_2_e), .f(bin_2_seteseg_2_f),
    .g(bin_2_seteseg_2_g));
  _7_Segment_Display u_7_segment_display_2 (
    .g(bin_2_seteseg_2_g), .f(bin_2_seteseg_2_f), .a(bin_2_seteseg_2_a_2), .b(bin_2_seteseg_2_b_2),
    .e(bin_2_seteseg_2_e), .d(bin_2_seteseg_2_d_2), .c(bin_2_seteseg_2_c_2));  // open: dp
endmodule

module \Contador_síncrono_M_a_N  (
  input  CLOCK,
  input  [3:0] N,
  input  [3:0] M,
  output out_4,
  output out_5,
  output out_6,
  output out_7
);

  wire bin_2_seteseg_1_a_2, bin_2_seteseg_1_b_2, bin_2_seteseg_1_c_2, bin_2_seteseg_1_d_2, bin_2_seteseg_1_e,
       bin_2_seteseg_1_f, bin_2_seteseg_1_g, bin_2_seteseg_2_a_2, bin_2_seteseg_2_b_2, bin_2_seteseg_2_c_2,
       bin_2_seteseg_2_d_2, bin_2_seteseg_2_e, bin_2_seteseg_2_f, bin_2_seteseg_2_g, bin_2_seteseg_3_a_2,
       bin_2_seteseg_3_b_2, bin_2_seteseg_3_c_2, bin_2_seteseg_3_d_2, bin_2_seteseg_3_e, bin_2_seteseg_3_f,
       bin_2_seteseg_3_g, jk_com_preset_e_clear_1_p1, jk_com_preset_e_clear_1_p3, jk_com_preset_e_clear_2_p1,
       jk_com_preset_e_clear_2_p3, jk_com_preset_e_clear_3_p1, jk_com_preset_e_clear_3_p3,
       jk_com_preset_e_clear_4_p1, jk_com_preset_e_clear_4_p3, LOAD_out, n0_a_n_comb_1_clear, n_a_0_1_p0,
       n_a_0_1_p1, n_a_0_1_p2, n_a_0_1_p3;
  wire [3:0] not_1_out;

  Button LOAD (.out(LOAD_out));
  n_a_0 n_a_0_1 (
    .LOAD(LOAD_out), .P3(n_a_0_1_p3), .P2(n_a_0_1_p2), .P1(n_a_0_1_p1), .P0(n_a_0_1_p0), .N3(not_1_out[3]),
    .N2(not_1_out[2]), .N1(not_1_out[1]), .N0(not_1_out[0]));  // open: C3, C2, C1, C0
  assign not_1_out = ~M;  // NOT_Gate not_1, 4 bits wide
  // JK_com_preset_e_clear jk_com_preset_e_clear_1: pin names not known; wires that end beside it: jk_com_preset_e_clear_1_p1, CLOCK, jk_com_preset_e_clear_1_p3, out_4
  // NOT_Gate not_2 has open pins: in=n0_a_n_comb_1_clear, out=open
  // NOT_Gate not_3 has open pins: in=n_a_0_1_p3, out=open
  // NOT_Gate not_4 has open pins: in=n_a_0_1_p2, out=open
  bin_2_seteseg bin_2_seteseg_1 (
    .D(M[3]), .C(M[2]), .B(M[1]), .A(M[0]), .a_2(bin_2_seteseg_1_a_2), .b_2(bin_2_seteseg_1_b_2),
    .c_2(bin_2_seteseg_1_c_2), .d_2(bin_2_seteseg_1_d_2), .e(bin_2_seteseg_1_e), .f(bin_2_seteseg_1_f),
    .g(bin_2_seteseg_1_g));
  // JK_com_preset_e_clear jk_com_preset_e_clear_2: pin names not known; wires that end beside it: jk_com_preset_e_clear_2_p1, CLOCK, jk_com_preset_e_clear_2_p3, out_5
  // NOT_Gate not_5 has open pins: in=n0_a_n_comb_1_clear, out=open
  _7_Segment_Display u_7_segment_display_1 (
    .g(bin_2_seteseg_1_g), .f(bin_2_seteseg_1_f), .a(bin_2_seteseg_1_a_2), .b(bin_2_seteseg_1_b_2),
    .e(bin_2_seteseg_1_e), .d(bin_2_seteseg_1_d_2), .c(bin_2_seteseg_1_c_2));  // open: dp
  // JK_com_preset_e_clear jk_com_preset_e_clear_3: pin names not known; wires that end beside it: jk_com_preset_e_clear_3_p1, CLOCK, jk_com_preset_e_clear_3_p3, out_6
  // NOT_Gate not_6 has open pins: in=n0_a_n_comb_1_clear, out=open
  // NOT_Gate not_7 has open pins: in=n_a_0_1_p1, out=open
  // NOT_Gate not_8 has open pins: in=n_a_0_1_p0, out=open
  // JK_com_preset_e_clear jk_com_preset_e_clear_4: pin names not known; wires that end beside it: jk_com_preset_e_clear_4_p1, CLOCK, jk_com_preset_e_clear_4_p3, out_7
  // NOT_Gate not_9 has open pins: in=n0_a_n_comb_1_clear, out=open
  _0_a_n_comb u_0_a_n_comb_1 (
    .CLEAR(n0_a_n_comb_1_clear), .Q3(out_7), .Q2(out_6), .Q1(out_5), .Q0(out_4), .N0(N[0]), .N1(N[1]),
    .N2(N[2]), .N3(N[3]));
  sinc_crescente_comb sinc_crescente_comb_1 (
    .Q0(out_7), .Q1(out_6), .Q2(out_5), .Q3(out_4), .J3(jk_com_preset_e_clear_4_p1),
    .K3(jk_com_preset_e_clear_4_p3), .J2(jk_com_preset_e_clear_3_p1), .K2(jk_com_preset_e_clear_3_p3),
    .J1(jk_com_preset_e_clear_2_p1), .K1(jk_com_preset_e_clear_2_p3), .J0(jk_com_preset_e_clear_1_p1),
    .K0(jk_com_preset_e_clear_1_p3));
  bin_2_seteseg bin_2_seteseg_2 (
    .D(N[3]), .C(N[2]), .B(N[1]), .A(N[0]), .a_2(bin_2_seteseg_2_a_2), .b_2(bin_2_seteseg_2_b_2),
    .c_2(bin_2_seteseg_2_c_2), .d_2(bin_2_seteseg_2_d_2), .e(bin_2_seteseg_2_e), .f(bin_2_seteseg_2_f),
    .g(bin_2_seteseg_2_g));
  bin_2_seteseg bin_2_seteseg_3 (
    .D(out_7), .C(out_6), .B(out_5), .A(out_4), .a_2(bin_2_seteseg_3_a_2), .b_2(bin_2_seteseg_3_b_2),
    .c_2(bin_2_seteseg_3_c_2), .d_2(bin_2_seteseg_3_d_2), .e(bin_2_seteseg_3_e), .f(bin_2_seteseg_3_f),
    .g(bin_2_seteseg_3_g));
  _7_Segment_Display u_7_segment_display_2 (
    .g(bin_2_seteseg_2_g), .f(bin_2_seteseg_2_f), .a(bin_2_seteseg_2_a_2), .b(bin_2_seteseg_2_b_2),
    .e(bin_2_seteseg_2_e), .d(bin_2_seteseg_2_d_2), .c(bin_2_seteseg_2_c_2));  // open: dp
  _7_Segment_Display u_7_segment_display_3 (
    .g(bin_2_seteseg_3_g), .f(bin_2_seteseg_3_f), .a(bin_2_seteseg_3_a_2), .b(bin_2_seteseg_3_b_2),
    .e(bin_2_seteseg_3_e), .d(bin_2_seteseg_3_d_2), .c(bin_2_seteseg_3_c_2));  // open: dp

  // Notes on the sheet:
  //   M
  //   N
  //   CONTAGEM
endmodule

module \Contador_síncrono_M_a_N_com_chave  (
  input  CHAVE,
  input  [3:0] M,
  input  [3:0] N,
  input  CLOCK,
  output out_5,
  output out_6,
  output out_7,
  output out_8
);

  wire bin_2_seteseg_1_a_2, bin_2_seteseg_1_b_2, bin_2_seteseg_1_c_2, bin_2_seteseg_1_d_2, bin_2_seteseg_1_e,
       bin_2_seteseg_1_f, bin_2_seteseg_1_g, bin_2_seteseg_2_a_2, bin_2_seteseg_2_b_2, bin_2_seteseg_2_c_2,
       bin_2_seteseg_2_d_2, bin_2_seteseg_2_e, bin_2_seteseg_2_f, bin_2_seteseg_2_g, bin_2_seteseg_3_a_2,
       bin_2_seteseg_3_b_2, bin_2_seteseg_3_c_2, bin_2_seteseg_3_d_2, bin_2_seteseg_3_e, bin_2_seteseg_3_f,
       bin_2_seteseg_3_g, jk_com_preset_e_clear_1_p4, jk_com_preset_e_clear_1_p5, jk_com_preset_e_clear_2_p4,
       jk_com_preset_e_clear_2_p5, jk_com_preset_e_clear_3_p4, jk_com_preset_e_clear_3_p5,
       jk_com_preset_e_clear_4_p4, jk_com_preset_e_clear_4_p5, LOAD_out, n0_a_n_comb_1_clear, n_a_0_1_p0,
       n_a_0_1_p1, n_a_0_1_p2, n_a_0_1_p3;
  wire [1:0] multiplexer_2_out, multiplexer_4_out, multiplexer_6_out, multiplexer_8_out,
       sinc_crescente_comb_1_j0, sinc_crescente_comb_1_j1, sinc_crescente_comb_1_j2,
       sinc_crescente_comb_1_j3, sinc_decrescente_comb_1_j0, sinc_decrescente_comb_1_j1,
       sinc_decrescente_comb_1_j2, sinc_decrescente_comb_1_j3;
  wire [3:0] multiplexer_1_out, multiplexer_10_out, not_1_out;

  n_a_0 n_a_0_1 (
    .LOAD(LOAD_out), .P3(n_a_0_1_p3), .P2(n_a_0_1_p2), .P1(n_a_0_1_p1), .P0(n_a_0_1_p0),
    .N3(multiplexer_1_out[3]), .N2(multiplexer_1_out[2]), .N1(multiplexer_1_out[1]), .N0(multiplexer_1_out[0]));  // open: C3, C2, C1, C0
  Multiplexer #(.width(4)) multiplexer_1 (.in0(not_1_out), .in1(M), .out(multiplexer_1_out), .sel(CHAVE));  // open: en
  assign not_1_out = ~M;  // NOT_Gate not_1, 4 bits wide
  Multiplexer #(.width(2)) multiplexer_2 (
    .in0(sinc_crescente_comb_1_j0), .in1(sinc_decrescente_comb_1_j0), .out(multiplexer_2_out), .sel(CHAVE));  // open: en
  // JK_com_preset_e_clear jk_com_preset_e_clear_1: pin names not known; wires that end beside it: multiplexer_2_out[0], CLOCK, multiplexer_2_out[1], jk_com_preset_e_clear_1_p4, jk_com_preset_e_clear_1_p5
  // NOT_Gate not_2 has open pins: in=n0_a_n_comb_1_clear, out=open
  // NOT_Gate not_3 has open pins: in=n_a_0_1_p3, out=open
  Button LOAD (.out(LOAD_out));
  Multiplexer multiplexer_3 (
    .in0(jk_com_preset_e_clear_1_p4), .in1(jk_com_preset_e_clear_1_p5), .out(out_5), .sel(CHAVE));  // open: en
  Multiplexer #(.width(2)) multiplexer_4 (
    .in0(sinc_crescente_comb_1_j1), .in1(sinc_decrescente_comb_1_j1), .out(multiplexer_4_out), .sel(CHAVE));  // open: en
  // JK_com_preset_e_clear jk_com_preset_e_clear_2: pin names not known; wires that end beside it: multiplexer_4_out[0], CLOCK, multiplexer_4_out[1], jk_com_preset_e_clear_2_p4, jk_com_preset_e_clear_2_p5
  // NOT_Gate not_4 has open pins: in=n0_a_n_comb_1_clear, out=open
  // NOT_Gate not_5 has open pins: in=n_a_0_1_p2, out=open
  bin_2_seteseg bin_2_seteseg_1 (
    .D(M[3]), .C(M[2]), .B(M[1]), .A(M[0]), .a_2(bin_2_seteseg_1_a_2), .b_2(bin_2_seteseg_1_b_2),
    .c_2(bin_2_seteseg_1_c_2), .d_2(bin_2_seteseg_1_d_2), .e(bin_2_seteseg_1_e), .f(bin_2_seteseg_1_f),
    .g(bin_2_seteseg_1_g));
  Multiplexer multiplexer_5 (
    .in0(jk_com_preset_e_clear_2_p4), .in1(jk_com_preset_e_clear_2_p5), .out(out_6), .sel(CHAVE));  // open: en
  _7_Segment_Display u_7_segment_display_1 (
    .g(bin_2_seteseg_1_g), .f(bin_2_seteseg_1_f), .a(bin_2_seteseg_1_a_2), .b(bin_2_seteseg_1_b_2),
    .e(bin_2_seteseg_1_e), .d(bin_2_seteseg_1_d_2), .c(bin_2_seteseg_1_c_2));  // open: dp
  Multiplexer #(.width(2)) multiplexer_6 (
    .in0(sinc_crescente_comb_1_j2), .in1(sinc_decrescente_comb_1_j2), .out(multiplexer_6_out), .sel(CHAVE));  // open: en
  // JK_com_preset_e_clear jk_com_preset_e_clear_3: pin names not known; wires that end beside it: multiplexer_6_out[0], CLOCK, multiplexer_6_out[1], jk_com_preset_e_clear_3_p4, jk_com_preset_e_clear_3_p5
  // NOT_Gate not_6 has open pins: in=n_a_0_1_p1, out=open
  // NOT_Gate not_7 has open pins: in=n0_a_n_comb_1_clear, out=open
  Multiplexer multiplexer_7 (
    .in0(jk_com_preset_e_clear_3_p4), .in1(jk_com_preset_e_clear_3_p5), .out(out_7), .sel(CHAVE));  // open: en
  bin_2_seteseg bin_2_seteseg_2 (
    .D(N[3]), .C(N[2]), .B(N[1]), .A(N[0]), .a_2(bin_2_seteseg_2_a_2), .b_2(bin_2_seteseg_2_b_2),
    .c_2(bin_2_seteseg_2_c_2), .d_2(bin_2_seteseg_2_d_2), .e(bin_2_seteseg_2_e), .f(bin_2_seteseg_2_f),
    .g(bin_2_seteseg_2_g));
  Multiplexer #(.width(2)) multiplexer_8 (
    .in0(sinc_crescente_comb_1_j3), .in1(sinc_decrescente_comb_1_j3), .out(multiplexer_8_out), .sel(CHAVE));  // open: en
  // JK_com_preset_e_clear jk_com_preset_e_clear_4: pin names not known; wires that end beside it: multiplexer_8_out[0], CLOCK, multiplexer_8_out[1], jk_com_preset_e_clear_4_p4, jk_com_preset_e_clear_4_p5
  // NOT_Gate not_8 has open pins: in=n0_a_n_comb_1_clear, out=open
  // NOT_Gate not_9 has open pins: in=n_a_0_1_p0, out=open
  _0_a_n_comb u_0_a_n_comb_1 (
    .CLEAR(n0_a_n_comb_1_clear), .Q3(out_8), .Q2(out_7), .Q1(out_6), .Q0(out_5), .N0(N[0]), .N1(N[1]),
    .N2(N[2]), .N3(N[3]));
  _7_Segment_Display u_7_segment_display_2 (
    .g(bin_2_seteseg_2_g), .f(bin_2_seteseg_2_f), .a(bin_2_seteseg_2_a_2), .b(bin_2_seteseg_2_b_2),
    .e(bin_2_seteseg_2_e), .d(bin_2_seteseg_2_d_2), .c(bin_2_seteseg_2_c_2));  // open: dp
  Multiplexer multiplexer_9 (
    .in0(jk_com_preset_e_clear_4_p4), .in1(jk_com_preset_e_clear_4_p5), .out(out_8), .sel(CHAVE));  // open: en
  Multiplexer #(.width(4)) multiplexer_10 (
    .in0({out_5, out_6, out_7, out_8}), .in1({out_5, out_6, out_7, out_8}), .out(multiplexer_10_out),
    .sel(CHAVE));  // open: en
  bin_2_seteseg bin_2_seteseg_3 (
    .D(out_8), .C(out_7), .B(out_6), .A(out_5), .a_2(bin_2_seteseg_3_a_2), .b_2(bin_2_seteseg_3_b_2),
    .c_2(bin_2_seteseg_3_c_2), .d_2(bin_2_seteseg_3_d_2), .e(bin_2_seteseg_3_e), .f(bin_2_seteseg_3_f),
    .g(bin_2_seteseg_3_g));
  sinc_decrescente_comb sinc_decrescente_comb_1 (
    .Q0(multiplexer_10_out[0]), .Q1(multiplexer_10_out[1]), .Q2(multiplexer_10_out[2]),
    .Q3(multiplexer_10_out[3]), .J3(sinc_decrescente_comb_1_j3[0]), .K3(sinc_decrescente_comb_1_j3[1]),
    .J2(sinc_decrescente_comb_1_j2[0]), .K2(sinc_decrescente_comb_1_j2[1]),
    .J1(sinc_decrescente_comb_1_j1[0]), .K1(sinc_decrescente_comb_1_j1[1]),
    .J0(sinc_decrescente_comb_1_j0[0]), .K0(sinc_decrescente_comb_1_j0[1]));
  sinc_crescente_comb sinc_crescente_comb_1 (
    .Q0(multiplexer_10_out[0]), .Q1(multiplexer_10_out[1]), .Q2(multiplexer_10_out[2]),
    .Q3(multiplexer_10_out[3]), .J3(sinc_crescente_comb_1_j3[0]), .K3(sinc_crescente_comb_1_j3[1]),
    .J2(sinc_crescente_comb_1_j2[0]), .K2(sinc_crescente_comb_1_j2[1]), .J1(sinc_crescente_comb_1_j1[0]),
    .K1(sinc_crescente_comb_1_j1[1]), .J0(sinc_crescente_comb_1_j0[0]), .K0(sinc_crescente_comb_1_j0[1]));
  _7_Segment_Display u_7_segment_display_3 (
    .g(bin_2_seteseg_3_g), .f(bin_2_seteseg_3_f), .a(bin_2_seteseg_3_a_2), .b(bin_2_seteseg_3_b_2),
    .e(bin_2_seteseg_3_e), .d(bin_2_seteseg_3_d_2), .c(bin_2_seteseg_3_c_2));  // open: dp

  // Other names for the same wires on the sheet: Q0 = out_8; Q1 = out_7; Q2 = out_6; Q3 = out_5

  // Notes on the sheet:
  //   M
  //   N
  //   1 = decrescente
  //   0 = crescente
  //   CONTAGEM
endmodule

module sinc_crescente_comb (
  input  Q0,
  input  Q1,
  input  Q2,
  input  Q3,
  output J3,
  output K3,
  output J2,
  output K2,
  output J1,
  output K1,
  output J0,
  output K0
);

  wire and_2_out, and_4_out, not_1_out, not_2_out, not_3_out;

  and and_1 (J3, Q1, Q2, Q3);
  not not_1 (not_1_out, Q0);
  and and_2 (and_2_out, Q1, Q2, Q3);
  and and_3 (J2, Q2, Q3);
  not not_2 (not_2_out, Q1);
  and and_4 (and_4_out, Q2, Q3);
  or or_1 (J1, Q3, Q2);
  not not_3 (not_3_out, Q2);
  or or_2 (K1, not_3_out, Q3);
  or or_3 (K3, not_1_out, and_2_out);
  or or_4 (K2, not_2_out, and_4_out);

  assign J0 = 1'b1;
  assign K0 = 1'b1;
endmodule

module sinc_decada_comb (
  input  Q0,
  input  Q1,
  input  Q2,
  input  Q3,
  output J3,
  output K3,
  output J2,
  output K2,
  output J1,
  output K1,
  output J0,
  output K0
);

  wire and_1_out, and_2_out, and_3_out, and_4_out, and_5_out, and_6_out, not_1_out, not_2_out, not_3_out;

  and and_1 (and_1_out, Q1, Q2, Q3);
  or or_1 (K3, Q3, Q2, Q1);
  and and_2 (and_2_out, Q2, Q3);
  and and_3 (and_3_out, Q0, Q2);
  not not_1 (not_1_out, Q1);
  and and_4 (and_4_out, Q2, Q3);
  not not_2 (not_2_out, Q0);
  and and_5 (and_5_out, not_2_out, Q3);
  and and_6 (and_6_out, Q0, Q1);
  not not_3 (not_3_out, Q2);
  or or_2 (K1, not_3_out, Q3, Q0);
  or or_3 (J3, and_1_out, Q0);
  or or_4 (J2, and_2_out, Q1, and_3_out);
  or or_5 (K2, not_1_out, and_4_out, Q0);
  or or_6 (J1, and_5_out, Q2, and_6_out);

  assign J0 = 1'b1;
  assign K0 = 1'b1;
endmodule

module sinc_decrescente_comb (
  input  Q0,
  input  Q1,
  input  Q2,
  input  Q3,
  output J3,
  output K3,
  output J2,
  output K2,
  output J1,
  output K1,
  output J0,
  output K0
);

  wire and_2_out, and_4_out, not_1_out, not_2_out, not_3_out, not_4_out, not_5_out, not_6_out, not_7_out,
       not_8_out, not_9_out, not_10_out, not_11_out, not_12_out, not_13_out;

  not not_1 (not_1_out, Q1);
  not not_2 (not_2_out, Q2);
  and and_1 (J3, not_1_out, not_2_out, not_3_out);
  not not_3 (not_3_out, Q3);
  not not_4 (not_4_out, Q1);
  and and_2 (and_2_out, not_4_out, not_5_out, not_6_out);
  not not_5 (not_5_out, Q2);
  not not_6 (not_6_out, Q3);
  not not_7 (not_7_out, Q2);
  and and_3 (J2, not_7_out, not_8_out);
  not not_8 (not_8_out, Q3);
  not not_9 (not_9_out, Q2);
  and and_4 (and_4_out, not_9_out, not_10_out);
  not not_10 (not_10_out, Q3);
  not not_11 (not_11_out, Q2);
  or or_1 (J1, not_11_out, not_12_out);
  not not_12 (not_12_out, Q3);
  not not_13 (not_13_out, Q3);
  or or_2 (K1, not_13_out, Q2);
  or or_3 (K3, and_2_out, Q0);
  or or_4 (K2, and_4_out, Q1);

  assign J0 = 1'b1;
  assign K0 = 1'b1;
endmodule

module _0_a_n_comb (
  input  Q3,
  input  Q2,
  input  Q1,
  input  Q0,
  input  N0,
  input  N1,
  input  N2,
  input  N3,
  output CLEAR
);

  wire xnor_1_out, xnor_2_out, xnor_3_out, xnor_4_out;

  nand nand_1 (CLEAR, xnor_1_out, xnor_2_out, xnor_3_out, xnor_4_out);
  xnor xnor_1 (xnor_1_out, Q0, N0);
  xnor xnor_2 (xnor_2_out, Q1, N1);
  xnor xnor_3 (xnor_3_out, Q2, N2);
  xnor xnor_4 (xnor_4_out, Q3, N3);
endmodule

module n_a_0 (
  input  LOAD,
  input  N3,
  input  N2,
  input  N1,
  input  N0,
  output P3,
  output C3,
  output P2,
  output C2,
  output P1,
  output C1,
  output P0,
  output C0
);

  wire not_1_out, not_2_out, not_3_out, not_4_out, not_5_out, not_6_out, not_7_out, not_8_out;

  nand nand_1 (P3, not_1_out, LOAD);
  not not_1 (not_1_out, N0);
  nand nand_2 (C3, not_2_out, LOAD);
  not not_2 (not_2_out, not_1_out);
  nand nand_3 (P2, not_4_out, LOAD);
  nand nand_4 (C2, not_3_out, LOAD);
  not not_3 (not_3_out, not_4_out);
  not not_4 (not_4_out, N1);
  nand nand_5 (P1, not_5_out, LOAD);
  not not_5 (not_5_out, N2);
  nand nand_6 (C1, not_6_out, LOAD);
  not not_6 (not_6_out, not_5_out);
  nand nand_7 (P0, not_8_out, LOAD);
  nand nand_8 (C0, not_7_out, LOAD);
  not not_7 (not_7_out, not_8_out);
  not not_8 (not_8_out, N3);
endmodule

module JK_com_sr_do_sistema (
  input  J,
  input  Clock,
  input  K,
  input  PRS,
  input  CLR,
  output Q,
  output nQ
);

  wire and_1_out, and_2_out;

  and and_1 (and_1_out, J, nQ);
  and and_2 (and_2_out, Q, K);
  S_R_Flip_Flop s_r_ff_1 (
    .S(and_1_out), .clk(Clock), .R(and_2_out), .Q(Q), .Qn(nQ), .preset(PRS), .reset(CLR));  // open: en
endmodule

module JK_sem_SR_do_sistema (
  input  J,
  input  CLOCK,
  input  K,
  input  PRS,
  input  CLR,
  output Q,
  output nQ
);

  wire nand_1_out, nand_2_out, nand_3_out, nand_4_out, nand_5_out, nand_6_out, not_1_out;

  nand nand_1 (nand_1_out, J, CLOCK, nQ);
  nand nand_2 (nand_2_out, Q, CLOCK, K);
  nand nand_3 (nand_3_out, PRS, nand_1_out, nand_4_out);
  nand nand_4 (nand_4_out, nand_3_out, nand_2_out, CLR);
  not not_1 (not_1_out, CLOCK);
  nand nand_5 (nand_5_out, nand_3_out, not_1_out);
  nand nand_6 (nand_6_out, not_1_out, nand_4_out);
  nand nand_7 (Q, PRS, nand_5_out, nQ);
  nand nand_8 (nQ, Q, nand_6_out, CLR);
endmodule

module M_a_N_chave_comb (
  input  LOAD,
  input  chave,
  input  N3,
  input  N2,
  input  N1,
  input  N0,
  output P3,
  output P2,
  output P1,
  output P0,
  output C3,
  output C2,
  output C1,
  output C0
);

  wire nand_1_out, nand_5_out, nand_8_out, nand_11_out, not_1_out, not_2_out, not_3_out, not_4_out,
       not_5_out, not_6_out, not_7_out, not_8_out;

  nand nand_1 (nand_1_out, not_1_out, LOAD);
  not not_1 (not_1_out, N0);
  nand nand_2 (P3, nand_1_out, chave);
  nand nand_3 (C3, not_2_out, LOAD);
  not not_2 (not_2_out, not_1_out);
  nand nand_4 (P2, nand_5_out, chave);
  nand nand_5 (nand_5_out, not_4_out, LOAD);
  nand nand_6 (C2, not_3_out, LOAD);
  not not_3 (not_3_out, not_4_out);
  not not_4 (not_4_out, N1);
  nand nand_7 (P1, nand_8_out, chave);
  nand nand_8 (nand_8_out, not_5_out, LOAD);
  not not_5 (not_5_out, N2);
  nand nand_9 (C1, not_6_out, LOAD);
  not not_6 (not_6_out, not_5_out);
  nand nand_10 (P0, nand_11_out, chave);
  nand nand_11 (nand_11_out, not_8_out, LOAD);
  nand nand_12 (C0, not_7_out, LOAD);
  not not_7 (not_7_out, not_8_out);
  not not_8 (not_8_out, N3);
endmodule

module _1_2_3_5_8_9_B_F_5 (
  input  Q0,
  input  Q1,
  input  Q2,
  input  Q3,
  output J3,
  output K3,
  output J2,
  output K2,
  output J1,
  output K1,
  output J0,
  output K0
);

  wire and_2_out, and_3_out, and_4_out, and_5_out, and_6_out, and_7_out, and_8_out, and_9_out, and_10_out,
       and_11_out, not_1_out, not_2_out, not_3_out, not_4_out, not_5_out, not_6_out, not_7_out, not_8_out,
       not_9_out, not_10_out, not_11_out, not_12_out, not_13_out, not_14_out, not_15_out;

  and and_1 (J3, Q1, not_1_out, Q3);
  not not_1 (not_1_out, Q2);
  and and_2 (and_2_out, Q2, not_2_out);
  not not_2 (not_2_out, Q3);
  not not_3 (not_3_out, Q0);
  and and_3 (and_3_out, not_3_out, not_4_out, not_5_out);
  not not_4 (not_4_out, Q2);
  not not_5 (not_5_out, Q3);
  and and_4 (and_4_out, Q2, Q3);
  and and_5 (and_5_out, Q0, Q2);
  not not_6 (not_6_out, Q0);
  and and_6 (and_6_out, not_6_out, not_7_out, Q3);
  not not_7 (not_7_out, Q1);
  not not_8 (not_8_out, Q0);
  and and_7 (and_7_out, not_8_out, not_9_out, Q3);
  not not_9 (not_9_out, Q2);
  not not_10 (not_10_out, Q1);
  and and_8 (and_8_out, not_10_out, Q3);
  not not_11 (not_11_out, Q0);
  and and_9 (and_9_out, not_11_out, Q2, Q3);
  not not_12 (not_12_out, Q0);
  and and_10 (and_10_out, not_12_out, Q3);
  and and_11 (and_11_out, Q0, not_13_out);
  not not_13 (not_13_out, Q3);
  not not_14 (not_14_out, Q0);
  and and_12 (K0, not_14_out, not_15_out);
  not not_15 (not_15_out, Q2);
  or or_1 (K3, and_2_out, Q1);
  or or_2 (J2, and_3_out, and_4_out, and_5_out);
  or or_3 (K2, and_6_out, and_7_out);
  or or_4 (J1, and_8_out, and_9_out);
  or or_5 (K1, and_10_out, Q1, and_11_out);

  assign J0 = 1'b1;
endmodule

module bin_2_seteseg (
  input  D,
  input  C,
  input  B,
  input  A,
  output a_2,
  output b_2,
  output c_2,
  output d_2,
  output e,
  output f,
  output g
);

  wire nand_1_out, nand_2_out, nand_3_out, nand_4_out, nand_5_out, nand_6_out, nand_7_out, nand_8_out,
       nand_9_out, nand_10_out, nand_11_out, nand_12_out, nand_13_out, nand_14_out, nand_15_out, nand_16_out,
       nand_17_out, nand_18_out, nand_19_out, nand_20_out, nand_21_out, nand_22_out, nand_23_out,
       nand_24_out, nand_25_out, nand_26_out, nand_27_out, nand_28_out, nand_29_out, nand_30_out,
       nand_31_out, nand_32_out, nand_33_out, nand_34_out, nand_35_out, nand_36_out, nand_37_out,
       nand_38_out, nand_39_out, nand_40_out, nand_41_out, nand_42_out, nand_43_out, nand_44_out,
       nand_45_out, nand_46_out, nand_47_out, nand_48_out, nand_49_out, nand_50_out, nand_51_out,
       nand_52_out, nand_53_out, nand_54_out, nand_55_out, nand_56_out, nand_57_out, nand_58_out,
       nand_59_out, nand_60_out, nand_61_out, nand_62_out, nand_63_out, nand_64_out, nand_65_out,
       nand_66_out, nand_67_out, nand_68_out, nand_69_out, nand_70_out, nand_71_out, nand_72_out,
       nand_73_out, nand_74_out, nand_75_out, nand_76_out, nand_77_out, nand_78_out, nand_79_out,
       nand_80_out, nand_81_out, nand_82_out, nand_83_out, nand_84_out, nand_85_out, nand_86_out,
       nand_87_out, nand_88_out, nand_89_out, nand_90_out, nand_91_out, nand_92_out, nand_93_out,
       nand_94_out, nand_95_out, nand_96_out, nand_97_out, nand_98_out, nand_99_out, nand_100_out,
       nand_101_out, nand_102_out, nand_103_out, nand_104_out, nand_106_out, nand_107_out, nand_108_out,
       nand_109_out, nand_110_out, nand_111_out, nand_112_out, nand_113_out, nand_114_out, nand_115_out,
       nand_116_out, nand_117_out, nand_118_out, nand_119_out, nand_120_out, nand_121_out, nand_122_out,
       nand_123_out, nand_124_out, nand_125_out, nand_126_out, nand_127_out, nand_128_out, nand_129_out,
       nand_130_out, nand_131_out, nand_132_out, nand_133_out, nand_134_out, nand_136_out, nand_137_out,
       nand_138_out, nand_139_out, nand_141_out, nand_142_out, nand_143_out, nand_144_out, nand_145_out,
       nand_146_out, nand_147_out, nand_148_out;

  nand nand_1 (nand_1_out, C, C);
  nand nand_2 (nand_2_out, D, D);
  nand nand_3 (nand_3_out, B, B);
  nand nand_4 (nand_4_out, D, D);
  nand nand_5 (nand_5_out, B, B);
  nand nand_6 (nand_6_out, D, D);
  nand nand_7 (nand_7_out, D, D);
  nand nand_8 (nand_8_out, C, C);
  nand nand_9 (nand_9_out, C, C);
  nand nand_10 (nand_10_out, C, C);
  nand nand_11 (nand_11_out, A, A);
  nand nand_12 (nand_12_out, A, A);
  nand nand_13 (nand_13_out, D, D);
  nand nand_14 (nand_14_out, C, C);
  nand nand_15 (nand_15_out, A, A);
  nand nand_16 (nand_16_out, D, D);
  nand nand_17 (nand_17_out, D, nand_1_out);
  nand nand_18 (nand_18_out, nand_2_out, nand_3_out);
  nand nand_19 (nand_19_out, nand_4_out, nand_5_out);
  nand nand_20 (nand_20_out, nand_6_out, A);
  nand nand_21 (nand_21_out, nand_7_out, nand_8_out);
  nand nand_22 (nand_22_out, nand_9_out, B);
  nand nand_23 (nand_23_out, nand_10_out, nand_11_out);
  nand nand_24 (nand_24_out, B, nand_12_out);
  nand nand_25 (nand_25_out, D, B);
  nand nand_26 (nand_26_out, D, C);
  nand nand_27 (nand_27_out, nand_13_out, C);
  nand nand_28 (nand_28_out, nand_14_out, B);
  nand nand_29 (nand_29_out, B, nand_15_out);
  nand nand_30 (nand_30_out, nand_16_out, C);
  nand nand_31 (nand_31_out, C, C);
  nand nand_32 (nand_32_out, A, A);
  nand nand_33 (nand_33_out, D, D);
  nand nand_34 (nand_34_out, D, D);
  nand nand_35 (nand_35_out, nand_17_out, nand_17_out);
  nand nand_36 (nand_36_out, B, B);
  nand nand_37 (nand_37_out, D, D);
  nand nand_38 (nand_38_out, C, C);
  nand nand_39 (nand_39_out, nand_18_out, nand_18_out);
  nand nand_40 (nand_40_out, A, A);
  nand nand_41 (nand_41_out, D, D);
  nand nand_42 (nand_42_out, B, B);
  nand nand_43 (nand_43_out, nand_19_out, nand_20_out);
  nand nand_44 (nand_44_out, B, B);
  nand nand_45 (nand_45_out, D, D);
  nand nand_46 (nand_46_out, C, C);
  nand nand_47 (nand_47_out, nand_21_out, nand_21_out);
  nand nand_48 (nand_48_out, A, A);
  nand nand_49 (nand_49_out, nand_22_out, nand_22_out);
  nand nand_50 (nand_50_out, B, B);
  nand nand_51 (nand_51_out, B, B);
  nand nand_52 (nand_52_out, nand_23_out, nand_24_out);
  nand nand_53 (nand_53_out, nand_25_out, nand_26_out);
  nand nand_54 (nand_54_out, B, B);
  nand nand_55 (nand_55_out, A, A);
  nand nand_56 (nand_56_out, nand_27_out, nand_27_out);
  nand nand_57 (nand_57_out, B, B);
  nand nand_58 (nand_58_out, nand_28_out, nand_29_out);
  nand nand_59 (nand_59_out, nand_30_out, nand_30_out);
  nand nand_60 (nand_60_out, B, B);
  nand nand_61 (nand_61_out, C, C);
  nand nand_62 (nand_62_out, nand_31_out, nand_32_out);
  nand nand_63 (nand_63_out, nand_33_out, B);
  nand nand_64 (nand_64_out, nand_34_out, C);
  nand nand_65 (nand_65_out, C, B);
  nand nand_66 (nand_66_out, nand_35_out, nand_36_out);
  nand nand_67 (nand_67_out, nand_37_out, nand_38_out);
  nand nand_68 (nand_68_out, nand_39_out, nand_40_out);
  nand nand_69 (nand_69_out, nand_41_out, B);
  nand nand_70 (nand_70_out, D, nand_42_out);
  nand nand_71 (nand_71_out, nand_43_out, nand_43_out);
  nand nand_72 (nand_72_out, nand_44_out, A);
  nand nand_73 (nand_73_out, nand_45_out, C);
  nand nand_74 (nand_74_out, D, nand_46_out);
  nand nand_75 (nand_75_out, nand_47_out, nand_48_out);
  nand nand_76 (nand_76_out, nand_49_out, A);
  nand nand_77 (nand_77_out, C, nand_50_out);
  nand nand_78 (nand_78_out, C, B);
  nand nand_79 (nand_79_out, D, nand_51_out);
  nand nand_80 (nand_80_out, nand_52_out, nand_52_out);
  nand nand_81 (nand_81_out, nand_53_out, nand_53_out);
  nand nand_82 (nand_82_out, nand_54_out, nand_55_out);
  nand nand_83 (nand_83_out, nand_56_out, nand_57_out);
  nand nand_84 (nand_84_out, nand_58_out, nand_58_out);
  nand nand_85 (nand_85_out, nand_59_out, nand_60_out);
  nand nand_86 (nand_86_out, D, nand_61_out);
  nand nand_87 (nand_87_out, D, A);
  nand nand_88 (nand_88_out, nand_62_out, nand_63_out);
  nand nand_89 (nand_89_out, nand_64_out, nand_64_out);
  nand nand_90 (nand_90_out, nand_65_out, nand_66_out);
  nand nand_91 (nand_91_out, A, A);
  nand nand_92 (nand_92_out, nand_67_out, nand_68_out);
  nand nand_93 (nand_93_out, C, C);
  nand nand_94 (nand_94_out, A, A);
  nand nand_95 (nand_95_out, nand_69_out, nand_69_out);
  nand nand_96 (nand_96_out, nand_70_out, nand_70_out);
  nand nand_97 (nand_97_out, nand_71_out, nand_72_out);
  nand nand_98 (nand_98_out, nand_73_out, nand_74_out);
  nand nand_99 (nand_99_out, nand_75_out, nand_76_out);
  nand nand_100 (nand_100_out, nand_77_out, nand_77_out);
  nand nand_101 (nand_101_out, nand_78_out, nand_78_out);
  nand nand_102 (nand_102_out, A, A);
  nand nand_103 (nand_103_out, nand_79_out, nand_79_out);
  nand nand_104 (nand_104_out, A, A);
  nand nand_105 (e, nand_80_out, nand_81_out);
  nand nand_106 (nand_106_out, nand_82_out, nand_83_out);
  nand nand_107 (nand_107_out, A, A);
  nand nand_108 (nand_108_out, C, C);
  nand nand_109 (nand_109_out, nand_84_out, nand_85_out);
  nand nand_110 (nand_110_out, nand_86_out, nand_87_out);
  nand nand_111 (nand_111_out, nand_88_out, nand_88_out);
  nand nand_112 (nand_112_out, nand_89_out, A);
  nand nand_113 (nand_113_out, nand_90_out, nand_90_out);
  nand nand_114 (nand_114_out, D, nand_91_out);
  nand nand_115 (nand_115_out, nand_92_out, nand_92_out);
  nand nand_116 (nand_116_out, nand_93_out, nand_94_out);
  nand nand_117 (nand_117_out, nand_95_out, A);
  nand nand_118 (nand_118_out, nand_96_out, A);
  nand nand_119 (nand_119_out, nand_97_out, nand_97_out);
  nand nand_120 (nand_120_out, nand_98_out, nand_98_out);
  nand nand_121 (nand_121_out, nand_99_out, nand_99_out);
  nand nand_122 (nand_122_out, nand_100_out, A);
  nand nand_123 (nand_123_out, nand_101_out, nand_102_out);
  nand nand_124 (nand_124_out, nand_103_out, nand_104_out);
  nand nand_125 (nand_125_out, nand_106_out, nand_106_out);
  nand nand_126 (nand_126_out, C, nand_107_out);
  nand nand_127 (nand_127_out, D, nand_108_out);
  nand nand_128 (nand_128_out, D, B);
  nand nand_129 (nand_129_out, nand_109_out, nand_109_out);
  nand nand_130 (nand_130_out, nand_110_out, nand_110_out);
  nand nand_131 (nand_131_out, nand_111_out, nand_112_out);
  nand nand_132 (nand_132_out, nand_113_out, nand_114_out);
  nand nand_133 (nand_133_out, nand_115_out, nand_116_out);
  nand nand_134 (nand_134_out, nand_117_out, nand_118_out);
  nand nand_135 (c_2, nand_119_out, nand_120_out);
  nand nand_136 (nand_136_out, nand_121_out, nand_122_out);
  nand nand_137 (nand_137_out, nand_123_out, nand_124_out);
  nand nand_138 (nand_138_out, nand_125_out, nand_126_out);
  nand nand_139 (nand_139_out, nand_127_out, nand_128_out);
  nand nand_140 (g, nand_129_out, nand_130_out);
  nand nand_141 (nand_141_out, nand_131_out, nand_131_out);
  nand nand_142 (nand_142_out, nand_132_out, nand_132_out);
  nand nand_143 (nand_143_out, nand_133_out, nand_133_out);
  nand nand_144 (nand_144_out, nand_134_out, nand_134_out);
  nand nand_145 (nand_145_out, nand_136_out, nand_136_out);
  nand nand_146 (nand_146_out, nand_137_out, nand_137_out);
  nand nand_147 (nand_147_out, nand_138_out, nand_138_out);
  nand nand_148 (nand_148_out, nand_139_out, nand_139_out);
  nand nand_149 (a_2, nand_141_out, nand_142_out);
  nand nand_150 (b_2, nand_143_out, nand_144_out);
  nand nand_151 (d_2, nand_145_out, nand_146_out);
  nand nand_152 (f, nand_147_out, nand_148_out);
endmodule

module _0_1_2_3_10_13_0 (
  input  Q3,
  input  Q2,
  input  Q1,
  input  Q0,
  output J3,
  output K3,
  output J2,
  output K2,
  output J1,
  output K1,
  output J0,
  output K0
);

  wire and_2_out, not_1_out;

  and and_1 (J3, Q1, Q0);
  not not_1 (not_1_out, Q2);
  and and_2 (and_2_out, not_1_out, Q0);
  not not_2 (K1, Q1);
  or or_1 (J1, and_2_out, Q1);

  assign J0 = 1'b1;
  assign J2 = Q2;
  assign K0 = 1'b1;
  assign K2 = 1'b1;
  assign K3 = Q0;
endmodule
